// Logisim project proj.circ as structural Verilog: 19 circuits, main circuit main
module addbit (
  input  a,
  input  b,
  input  c,
  output s,
  output o
);

  wire and_1_out, and_2_out, xor_1_out;

  and and_1 (and_1_out, a, b);
  xor xor_1 (xor_1_out, a, b);
  xor xor_2 (s, xor_1_out, c);
  and and_2 (and_2_out, xor_1_out, c);
  or or_1 (o, and_1_out, and_2_out);

  // Notes on the sheet:
  //   Adiciona dois bits com carry
  //   e passa o proximo carry
  //   a ^ b ^ c
  //   ab + c(a ^ b)
endmodule

module checkoverflow (
  input  sig_a,
  input  sig_b,
  input  sig_s,
  output overflow
);

  wire xnor_1_out, xor_1_out;

  xnor xnor_1 (xnor_1_out, sig_a, sig_b);
  xor xor_1 (xor_1_out, sig_b, sig_s);
  and and_1 (overflow, xnor_1_out, xor_1_out);

  // Notes on the sheet:
  //   Verifica overflow atraves dos sinais
endmodule

module main (
  input  x4,
  input  x3,
  input  x2,
  input  x1,
  input  x0
);

  wire button_2_out, button_3_out, button_out, interface_1_out_12, interface_1_out_13, interface_1_out_14,
       interface_1_out_15, interface_1_out_16, interface_1_out_17, interface_1_out_18, interface_1_out_19,
       interface_1_out_20, interface_1_out_22, interface_1_out_23, interface_1_out_24, interface_1_out_25,
       interface_1_out_26, interface_1_out_27, interface_1_out_28, interface_1_out_29, interface_1_out_30,
       interface_1_overflow, set_out, x_out, zero_out;

  Button zero (.out(zero_out));
  Button set (.out(set_out));
  Button button (.out(button_out));
  Button button_2 (.out(button_2_out));
  Button x (.out(x_out));
  Button button_3 (.out(button_3_out));
  LED #(.active("true")) OVERFLOW (.in(interface_1_overflow));
  \interface  interface_1 (
    .x4(x4), .x3(x3), .x2(x2), .x1(x1), .x0(x0), .zero(zero_out), .set(set_out), .plus(button_out),
    .minus(button_2_out), .times(x_out), .equals(button_3_out), .OVERFLOW(interface_1_overflow),
    .out_12(interface_1_out_12), .out_13(interface_1_out_13), .out_14(interface_1_out_14),
    .out_15(interface_1_out_15), .out_16(interface_1_out_16), .out_17(interface_1_out_17),
    .out_18(interface_1_out_18), .out_19(interface_1_out_19), .out_20(interface_1_out_20),
    .out_22(interface_1_out_22), .out_23(interface_1_out_23), .out_24(interface_1_out_24),
    .out_25(interface_1_out_25), .out_26(interface_1_out_26), .out_27(interface_1_out_27),
    .out_28(interface_1_out_28), .out_29(interface_1_out_29), .out_30(interface_1_out_30));
  _7_Segment_Display #(.active("true")) u_7_segment_display_1 (.g(interface_1_out_12));  // open: f, a, b, e, d, c, dp
  _7_Segment_Display #(.active("true")) u_7_segment_display_2 (.g(interface_1_out_22));  // open: f, a, b, e, d, c, dp
  _7_Segment_Display #(.active("true")) u_7_segment_display_3 (
    .b(interface_1_out_13), .c(interface_1_out_13));  // open: g, f, a, e, d, dp
  _7_Segment_Display #(.active("true")) u_7_segment_display_4 (
    .b(interface_1_out_23), .c(interface_1_out_23));  // open: g, f, a, e, d, dp
  _7_Segment_Display #(.active("true")) u_7_segment_display_5 (
    .g(interface_1_out_14), .f(interface_1_out_15), .a(interface_1_out_16), .b(interface_1_out_17),
    .e(interface_1_out_18), .d(interface_1_out_19), .c(interface_1_out_20));  // open: dp
  _7_Segment_Display #(.active("true")) u_7_segment_display_6 (
    .g(interface_1_out_24), .f(interface_1_out_25), .a(interface_1_out_26), .b(interface_1_out_27),
    .e(interface_1_out_28), .d(interface_1_out_29), .c(interface_1_out_30));  // open: dp

  // Notes on the sheet:
  //   Numero de entrada na
  //   na representacao binaria
  //   Operacoes
  //   Executa a operacao
  //   Numero da entrada
  //   Numero na memoria
endmodule

module display (
  input  s4,
  input  s3,
  input  s2,
  input  s1,
  input  s0,
  output signal,
  output one,
  output d0,
  output d1,
  output d2,
  output d3,
  output d4,
  output d5,
  output d6
);

  wire and_1_out, and_2_out, and_3_out, and_4_out, and_5_out, and_6_out, and_7_out, and_8_out, and_9_out,
       and_10_out, and_11_out, and_12_out, and_13_out, and_14_out, and_15_out, and_16_out, and_17_out,
       and_18_out, and_19_out, and_20_out, and_21_out, and_22_out, and_23_out, and_24_out, and_25_out,
       and_26_out, and_27_out, and_28_out, not_1_out, not_2_out, not_3_out, not_4_out, not_5_out, or_2_out,
       or_4_out, or_6_out, or_7_out, or_10_out, or_11_out, or_12_out, or_13_out, or_14_out, or_16_out,
       or_17_out, or_19_out, or_22_out, or_23_out, or_24_out, or_25_out, or_26_out, or_27_out;

  not not_1 (not_1_out, s3);
  not not_2 (not_2_out, s4);
  not not_3 (not_3_out, s1);
  not not_4 (not_4_out, s2);
  not not_5 (not_5_out, s0);
  or or_1 (signal, and_7_out, and_12_out, and_14_out, and_15_out, or_2_out);
  and and_1 (and_1_out, s4, not_1_out, s2, s1, s0);
  and and_2 (and_2_out, 1'b1, not_1_out, not_4_out, s1, s0);
  and and_3 (and_3_out, not_2_out, s3, not_4_out, s1, 1'b1);
  and and_4 (and_4_out, not_2_out, s3, s2, not_3_out, not_5_out);
  and and_5 (and_5_out, s4, not_1_out, 1'b1, not_3_out, 1'b1);
  and and_6 (and_6_out, not_2_out, s3, s2, 1'b1, s0);
  and and_7 (and_7_out, s4, not_1_out, not_4_out, 1'b1, 1'b1);
  and and_8 (and_8_out, not_2_out, not_1_out, s2, not_3_out, not_5_out);
  and and_9 (and_9_out, not_2_out, 1'b1, not_4_out, not_3_out, 1'b1);
  and and_10 (and_10_out, 1'b1, s3, s2, 1'b1, not_5_out);
  and and_11 (and_11_out, 1'b1, not_1_out, not_4_out, s1, 1'b1);
  and and_12 (and_12_out, s4, s3, 1'b1, s1, not_5_out);
  and and_13 (and_13_out, not_2_out, s3, s2, s1, 1'b1);
  and and_14 (and_14_out, s4, s3, 1'b1, not_3_out, s0);
  and and_15 (and_15_out, s4, 1'b1, s2, 1'b1, s0);
  and and_16 (and_16_out, not_2_out, not_1_out, 1'b1, s1, not_5_out);
  and and_17 (and_17_out, not_2_out, not_1_out, s2, not_3_out, s0);
  and and_18 (and_18_out, not_2_out, s3, not_4_out, not_3_out, 1'b1);
  and and_19 (and_19_out, 1'b1, s3, s2, not_3_out, s0);
  or or_2 (or_2_out, and_20_out, and_21_out, and_23_out, and_28_out, 1'b0);
  and and_20 (and_20_out, s4, not_1_out, s2, not_3_out, not_5_out);
  and and_21 (and_21_out, s4, not_1_out, 1'b1, s1, not_5_out);
  and and_22 (and_22_out, 1'b1, not_1_out, 1'b1, s1, s0);
  and and_23 (and_23_out, s4, s3, 1'b1, not_3_out, not_5_out);
  and and_24 (and_24_out, 1'b1, not_1_out, s2, s1, not_5_out);
  and and_25 (and_25_out, 1'b1, 1'b1, not_4_out, not_3_out, not_5_out);
  and and_26 (and_26_out, 1'b1, s3, not_4_out, 1'b1, not_5_out);
  and and_27 (and_27_out, s4, not_1_out, not_4_out, not_3_out, 1'b1);
  and and_28 (and_28_out, s4, s3, not_4_out, s1, 1'b1);
  or or_3 (one, and_3_out, and_4_out, and_5_out, and_6_out, or_4_out);
  or or_4 (or_4_out, and_7_out, and_13_out, and_21_out);
  or or_5 (d0, and_1_out, and_8_out, and_10_out, and_11_out, or_6_out);
  or or_6 (or_6_out, and_13_out, and_16_out, and_17_out, and_18_out, or_7_out);
  or or_7 (or_7_out, and_19_out, and_20_out, and_23_out, and_27_out, and_28_out);
  or or_8 (d1, and_1_out, and_8_out, and_13_out, and_17_out, or_11_out);
  or or_9 (d2, and_4_out, and_6_out, and_12_out, and_14_out, or_10_out);
  or or_10 (or_10_out, and_16_out, and_17_out, and_18_out, and_20_out, or_12_out);
  or or_11 (or_11_out, and_18_out, and_21_out, and_23_out, and_24_out, or_13_out);
  or or_12 (or_12_out, and_22_out, and_24_out, and_25_out, and_26_out, or_14_out);
  or or_13 (or_13_out, and_25_out, and_26_out, and_27_out, and_28_out, 1'b0);
  or or_14 (or_14_out, and_27_out, and_28_out);
  or or_15 (d3, and_3_out, and_8_out, and_9_out, and_10_out, or_16_out);
  or or_16 (or_16_out, and_11_out, and_14_out, and_15_out, and_19_out, or_17_out);
  or or_17 (or_17_out, and_20_out, and_21_out, and_22_out, and_23_out, 1'b0);
  or or_18 (d4, and_4_out, and_12_out, and_16_out, and_20_out, or_19_out);
  or or_19 (or_19_out, and_24_out, and_25_out, and_26_out);
  or or_20 (d6, and_3_out, and_8_out, and_9_out, and_13_out, or_23_out);
  or or_21 (d5, and_1_out, and_2_out, and_4_out, and_6_out, or_22_out);
  or or_22 (or_22_out, and_12_out, and_16_out, and_17_out, and_18_out, or_24_out);
  or or_23 (or_23_out, and_14_out, and_15_out, and_17_out, and_19_out, or_25_out);
  or or_24 (or_24_out, and_19_out, and_20_out, and_24_out, and_25_out, or_26_out);
  or or_25 (or_25_out, and_21_out, and_22_out, and_23_out, and_24_out, or_27_out);
  or or_26 (or_26_out, and_26_out, and_27_out, and_28_out);
  or or_27 (or_27_out, and_27_out, and_28_out);

  // Notes on the sheet:
  //   -1101
  //   10111
  //   -0011
  //   0101-
  //   01100
  //   10-0-
  //   011-1
  //   100--
  //   00100
  //   0-00-
  //   -11-0
  //   -001-
  //   11-10
  //   0111-
  //   11-01
  //   1-1-1
  //   00-10
  //   00101
  //   0100-
  //   10100
  //   10-10
  //   -0-11
  //   11-00
  //   -0110
  //   --000
  //   -10-0
  //   1000-
  //   1101-
  //   Circuito PLA que transforma um
  //   numero em binario em um display
  //   de 7 segmentos
endmodule

module sum (
  input  a4,
  input  a3,
  input  a2,
  input  a1,
  input  a0,
  input  b4,
  input  b3,
  input  b2,
  input  b1,
  input  b0,
  output OVERFLOW,
  output carry,
  output s4,
  output s3,
  output s2,
  output s1,
  output s0
);

  wire addbit_2_o, addbit_3_o, addbit_4_o, addbit_5_o;

  addbit addbit_1 (.a(a4), .b(b4), .o(carry), .c(addbit_2_o), .s(s4));
  addbit addbit_2 (.a(a3), .b(b3), .o(addbit_2_o), .c(addbit_3_o), .s(s3));
  addbit addbit_3 (.a(a2), .b(b2), .o(addbit_3_o), .c(addbit_4_o), .s(s2));
  addbit addbit_4 (.a(a1), .b(b1), .o(addbit_4_o), .c(addbit_5_o), .s(s1));
  addbit addbit_5 (.a(a0), .b(b0), .o(addbit_5_o), .c(1'b0), .s(s0));
  checkoverflow checkoverflow_1 (.sig_a(a4), .sig_b(b4), .sig_s(s4), .overflow(OVERFLOW));

  // Notes on the sheet:
  //   Realiza a soma de
  //   dois numeros de 5 bits
endmodule

module register (
  input  clock,
  input  x4,
  input  x3,
  input  x2,
  input  x1,
  input  x0,
  output y4,
  output y3,
  output y2,
  output y1,
  output y0
);

  D_Flip_Flop #(.trigger("rising")) d_ff_1 (.clk(clock), .D(x4), .Q(y4));  // open: Qn, preset, en, reset
  D_Flip_Flop #(.trigger("rising")) d_ff_2 (.clk(clock), .D(x3), .Q(y3));  // open: Qn, preset, en, reset
  D_Flip_Flop #(.trigger("rising")) d_ff_3 (.clk(clock), .D(x2), .Q(y2));  // open: Qn, preset, en, reset
  D_Flip_Flop #(.trigger("rising")) d_ff_4 (.clk(clock), .D(x1), .Q(y1));  // open: Qn, preset, en, reset
  D_Flip_Flop #(.trigger("rising")) d_ff_5 (.clk(clock), .D(x0), .Q(y0));  // open: Qn, preset, en, reset

  // Notes on the sheet:
  //   Memoria de 5 bits
  //   Os bits da entrada sao armazenados
  //   na subida do clock
endmodule

module \interface  (
  input  x4,
  input  x3,
  input  x2,
  input  x1,
  input  x0,
  input  zero,
  input  set,
  input  plus,
  input  minus,
  input  times,
  input  equals,
  output out_12,
  output out_13,
  output out_14,
  output out_15,
  output out_16,
  output out_17,
  output out_18,
  output out_19,
  output out_20,
  output OVERFLOW,
  output out_22,
  output out_23,
  output out_24,
  output out_25,
  output out_26,
  output out_27,
  output out_28,
  output out_29,
  output out_30
);

  wire operation_1_o0, operation_1_o1, operation_1_o2, processor_1_m0, processor_1_m1, processor_1_m2,
       processor_1_m3, processor_1_m4, processor_1_overflow, register_1_y0, register_1_y1, register_1_y2,
       register_1_y3, register_1_y4;

  operation operation_1 (
    .zero(zero), .set(set), .in_3(plus), .in_4(minus), .x(times), .o2(operation_1_o2), .o1(operation_1_o1),
    .o0(operation_1_o0));
  register register_1 (
    .x4(processor_1_m4), .x3(processor_1_m3), .x2(processor_1_m2), .x1(processor_1_m1), .x0(processor_1_m0),
    .clock(equals), .y4(register_1_y4), .y3(register_1_y3), .y2(register_1_y2), .y1(register_1_y1),
    .y0(register_1_y0));
  processor processor_1 (
    .m4(processor_1_m4), .m3(processor_1_m3), .m2(processor_1_m2), .m1(processor_1_m1), .m0(processor_1_m0),
    .o2(operation_1_o2), .o1(operation_1_o1), .o0(operation_1_o0), .x4(x4), .x3(x3), .x2(x2), .x1(x1),
    .x0(x0), .y4(register_1_y4), .y3(register_1_y3), .y2(register_1_y2), .y1(register_1_y1),
    .y0(register_1_y0), .OVERFLOW(processor_1_overflow));
  D_Flip_Flop #(.trigger("rising")) d_ff_1 (
    .clk(equals), .D(processor_1_overflow), .Q(OVERFLOW));  // open: Qn, preset, en, reset
  display display_1 (
    .s4(x4), .s3(x3), .s2(x2), .s1(x1), .s0(x0), .signal(out_12), .one(out_13), .d0(out_14), .d1(out_15),
    .d2(out_16), .d3(out_17), .d4(out_18), .d5(out_19), .d6(out_20));
  display display_2 (
    .s4(register_1_y4), .s3(register_1_y3), .s2(register_1_y2), .s1(register_1_y1), .s0(register_1_y0),
    .signal(out_22), .one(out_23), .d0(out_24), .d1(out_25), .d2(out_26), .d3(out_27), .d4(out_28),
    .d5(out_29), .d6(out_30));

  // Notes on the sheet:
  //   Comando principal
  //   Calcula o resultado
  //   Numeros da entrada
  //   Armazenador de operacoes
  //   Memoria da calculadora
  //   Interface da calculadora
  //   O overflow precisa de um flip-flop
  //   para sincronizar a exibicao do resultado
  //   com a exibicao do overflow
  //   Saidas com as exibicoes
  //   dos valores em displays de
  //   sete segmentos
endmodule

module codif (
  input  s0,
  input  s1,
  input  s2,
  input  s3,
  input  s4,
  output o2,
  output o1,
  output o0
);

  or or_1 (o1, s3, s2);
  or or_2 (o0, s1, s3);

  assign o2 = s4;

  // Notes on the sheet:
  //   Coficador 5 para 3
endmodule

module operation (
  input  zero,
  input  set,
  input  in_3,
  input  in_4,
  input  x,
  output o2,
  output o1,
  output o0
);

  wire or_1_out, register_1_y0, register_1_y1, register_1_y2, register_1_y3, register_1_y4;

  or or_1 (or_1_out, zero, set, in_3, in_4, x);
  register register_1 (
    .x4(zero), .x3(set), .x2(in_3), .x1(in_4), .x0(x), .clock(or_1_out), .y4(register_1_y4),
    .y3(register_1_y3), .y2(register_1_y2), .y1(register_1_y1), .y0(register_1_y0));
  codif codif_1 (
    .s0(register_1_y4), .s1(register_1_y3), .s2(register_1_y2), .s3(register_1_y1), .s4(register_1_y0),
    .o2(o2), .o1(o1), .o0(o0));

  // Notes on the sheet:
  //   Ativa a operacao selecionada
endmodule

module processor (
  input  x4,
  input  x3,
  input  x2,
  input  x1,
  input  x0,
  input  y4,
  input  y3,
  input  y2,
  input  y1,
  input  y0,
  input  o2,
  input  o1,
  input  o0,
  output m4,
  output m3,
  output m2,
  output m1,
  output m0,
  output OVERFLOW
);

  wire mul_1_overflow, mul_1_s0, mul_1_s1, mul_1_s2, mul_1_s3, mul_1_s4, sub_1_overflow, sub_1_s0, sub_1_s1,
       sub_1_s2, sub_1_s3, sub_1_s4, sum_1_carry, sum_1_overflow, sum_1_s0, sum_1_s1, sum_1_s2, sum_1_s3,
       sum_1_s4;

  LED #(.active("true")) led_1 (.in(sum_1_carry));
  sum sum_1 (
    .a4(x4), .a3(x3), .a2(x2), .a1(x1), .a0(x0), .b4(y4), .b3(y3), .b2(y2), .b1(y1), .b0(y0),
    .carry(sum_1_carry), .OVERFLOW(sum_1_overflow), .s4(sum_1_s4), .s3(sum_1_s3), .s2(sum_1_s2),
    .s1(sum_1_s1), .s0(sum_1_s0));
  sub sub_1 (
    .a4(x4), .a3(x3), .a2(x2), .a1(x1), .a0(x0), .b4(y4), .b3(y3), .b2(y2), .b1(y1), .b0(y0),
    .OVERFLOW(sub_1_overflow), .s4(sub_1_s4), .s3(sub_1_s3), .s2(sub_1_s2), .s1(sub_1_s1), .s0(sub_1_s0));
  mul mul_1 (
    .a4(x4), .a3(x3), .a2(x2), .a1(x1), .a0(x0), .b4(y4), .b3(y3), .b2(y2), .b1(y1), .b0(y0),
    .OVERFLOW(mul_1_overflow), .s4(mul_1_s4), .s3(mul_1_s3), .s2(mul_1_s2), .s1(mul_1_s1), .s0(mul_1_s0));
  mux5 mux5_1 (.a(1'b0), .b(x4), .c(sum_1_s4), .d(sub_1_s4), .e(mul_1_s4), .s2(o2), .s1(o1), .s0(o0), .mux(m4));
  mux5 mux5_2 (.a(1'b0), .b(x3), .c(sum_1_s3), .d(sub_1_s3), .e(mul_1_s3), .s2(o2), .s1(o1), .s0(o0), .mux(m3));
  mux5 mux5_3 (.a(1'b0), .b(x2), .c(sum_1_s2), .d(sub_1_s2), .e(mul_1_s2), .s2(o2), .s1(o1), .s0(o0), .mux(m2));
  mux5 mux5_4 (.a(1'b0), .b(x1), .c(sum_1_s1), .d(sub_1_s1), .e(mul_1_s1), .s2(o2), .s1(o1), .s0(o0), .mux(m1));
  mux5 mux5_5 (.a(1'b0), .b(x0), .c(sum_1_s0), .d(sub_1_s0), .e(mul_1_s0), .s2(o2), .s1(o1), .s0(o0), .mux(m0));
  mux5 mux5_6 (
    .a(1'b0), .b(1'b0), .c(sum_1_overflow), .d(sub_1_overflow), .e(mul_1_overflow), .s2(o2), .s1(o1),
    .s0(o0), .mux(OVERFLOW));

  // Notes on the sheet:
  //   Central de processamento
  //   Aqui todas as contas sao feitas, e de
  //   acordo com a operacao selecionada, o
  //   resultado adequado e' escolhido por multiplexadores.
endmodule

module mux5 (
  input  a,
  input  b,
  input  c,
  input  d,
  input  e,
  input  s2,
  input  s1,
  input  s0,
  output mux
);

  wire and_1_out, and_2_out, and_3_out, and_4_out, and_5_out, and_6_out, and_7_out, and_8_out, and_9_out,
       and_10_out, not_1_out, not_2_out, not_3_out;

  not not_1 (not_1_out, s0);
  not not_2 (not_2_out, s1);
  not not_3 (not_3_out, s2);
  and and_1 (and_1_out, not_3_out, a, not_2_out);
  and and_2 (and_2_out, not_3_out, b, not_2_out);
  and and_3 (and_3_out, not_3_out, c, s1);
  and and_4 (and_4_out, not_3_out, d, s1);
  and and_5 (and_5_out, s2, e, not_2_out);
  and and_6 (and_6_out, and_1_out, not_1_out);
  and and_7 (and_7_out, and_2_out, s0);
  and and_8 (and_8_out, and_3_out, not_1_out);
  and and_9 (and_9_out, and_4_out, s0);
  and and_10 (and_10_out, and_5_out, not_1_out);
  or or_1 (mux, and_6_out, and_7_out, and_8_out, and_9_out, and_10_out);

  // Notes on the sheet:
  //   Multiplexador 5 para 1
endmodule

module sub (
  input  a4,
  input  a3,
  input  a2,
  input  a1,
  input  a0,
  input  b4,
  input  b3,
  input  b2,
  input  b1,
  input  b0,
  output s4,
  output s3,
  output s2,
  output s1,
  output s0,
  output OVERFLOW
);

  wire neg_1_y0, neg_1_y1, neg_1_y2, neg_1_y3, neg_1_y4;

  neg neg_1 (
    .x4(a4), .x3(a3), .x2(a2), .x1(a1), .x0(a0), .y4(neg_1_y4), .y3(neg_1_y3), .y2(neg_1_y2), .y1(neg_1_y1),
    .y0(neg_1_y0));
  sum sum_1 (
    .a4(neg_1_y4), .a3(neg_1_y3), .a2(neg_1_y2), .a1(neg_1_y1), .a0(neg_1_y0), .b4(b4), .b3(b3), .b2(b2),
    .b1(b1), .b0(b0), .OVERFLOW(OVERFLOW), .s4(s4), .s3(s3), .s2(s2), .s1(s1), .s0(s0));  // open: carry

  // Notes on the sheet:
  //   Realiza a subtracao de dois
  //   numeros de 5 bits
endmodule

module neg (
  input  x4,
  input  x3,
  input  x2,
  input  x1,
  input  x0,
  output y4,
  output y3,
  output y2,
  output y1,
  output y0
);

  wire not_1_out, not_2_out, not_3_out, not_4_out, not_5_out, not_6_out;

  not not_1 (not_1_out, x4);
  not not_2 (not_2_out, x3);
  not not_3 (not_3_out, x2);
  not not_4 (not_4_out, x1);
  not not_5 (not_5_out, x0);
  sum sum_1 (
    .a4(not_1_out), .a3(not_2_out), .a2(not_3_out), .a1(not_4_out), .a0(not_5_out), .b4(1'b0), .b3(1'b0),
    .b2(1'b0), .b1(1'b0), .b0(not_6_out), .s4(y4), .s3(y3), .s2(y2), .s1(y1), .s0(y0));  // open: carry, OVERFLOW
  not not_6 (not_6_out, 1'b0);

  // Notes on the sheet:
  //   numero de 5 bits
  //   Inverte o sinal de um
endmodule

module mul (
  input  a4,
  input  a3,
  input  a2,
  input  a1,
  input  a0,
  input  b4,
  input  b3,
  input  b2,
  input  b1,
  input  b0,
  output s4,
  output s3,
  output s2,
  output s1,
  output s0,
  output OVERFLOW
);

  wire muxsignal_1_s0, muxsignal_1_s1, muxsignal_1_s2, muxsignal_1_s3, muxsignal_1_s4, muxsignal_2_s0,
       muxsignal_2_s1, muxsignal_2_s2, muxsignal_2_s3, muxsignal_2_s4;

  muxsignal muxsignal_1 (
    .x4(a4), .x3(a3), .x2(a2), .x1(a1), .x0(a0), .signal(b4), .s4(muxsignal_1_s4), .s3(muxsignal_1_s3),
    .s2(muxsignal_1_s2), .s1(muxsignal_1_s1), .s0(muxsignal_1_s0));
  muxsignal muxsignal_2 (
    .x4(b4), .x3(b3), .x2(b2), .x1(b1), .x0(b0), .signal(b4), .s4(muxsignal_2_s4), .s3(muxsignal_2_s3),
    .s2(muxsignal_2_s2), .s1(muxsignal_2_s1), .s0(muxsignal_2_s0));
  innermul innermul_1 (
    .a4(muxsignal_1_s4), .a3(muxsignal_1_s3), .a2(muxsignal_1_s2), .a1(muxsignal_1_s1), .a0(muxsignal_1_s0),
    .b4(muxsignal_2_s4), .b3(muxsignal_2_s3), .b2(muxsignal_2_s2), .b1(muxsignal_2_s1), .b0(muxsignal_2_s0),
    .out_11(s4), .out_12(s3), .out_13(s2), .out_14(s1), .out_15(s0), .out_16(OVERFLOW));

  // Notes on the sheet:
  //   Realiza a multiplicacao de
  //   dois numeros de cinco bits
endmodule

module shiftleft (
  input  x4,
  input  x3,
  input  x2,
  input  x1,
  input  x0,
  input  set,
  input  clock,
  output x4_2,
  output x3_2,
  output x2_2,
  output x1_2,
  output x0_2
);

  wire and_1_out, and_2_out, and_3_out, and_4_out, and_5_out, and_6_out, and_7_out, and_8_out, and_9_out,
       not_1_out, not_2_out, not_3_out, not_4_out, or_1_out, or_2_out, or_3_out, or_4_out;

  not not_1 (not_1_out, set);
  and and_1 (and_1_out, not_1_out, x3_2);
  and and_2 (and_2_out, set, x4);
  or or_1 (or_1_out, and_2_out, and_1_out);
  D_Flip_Flop #(.trigger("rising")) d_ff_1 (.clk(clock), .D(or_1_out), .Q(x4_2));  // open: Qn, preset, en, reset
  not not_2 (not_2_out, set);
  and and_3 (and_3_out, set, x3);
  and and_4 (and_4_out, not_2_out, x2_2);
  or or_2 (or_2_out, and_3_out, and_4_out);
  and and_5 (and_5_out, set, x2);
  or or_3 (or_3_out, and_5_out, and_6_out);
  D_Flip_Flop #(.trigger("rising")) d_ff_2 (.clk(clock), .D(or_2_out), .Q(x3_2));  // open: Qn, preset, en, reset
  not not_3 (not_3_out, set);
  and and_6 (and_6_out, not_3_out, x1_2);
  D_Flip_Flop #(.trigger("rising")) d_ff_3 (.clk(clock), .D(or_3_out), .Q(x2_2));  // open: Qn, preset, en, reset
  not not_4 (not_4_out, set);
  and and_7 (and_7_out, set, x1);
  and and_8 (and_8_out, not_4_out, x0_2);
  or or_4 (or_4_out, and_7_out, and_8_out);
  and and_9 (and_9_out, x0, set);
  D_Flip_Flop #(.trigger("rising")) d_ff_4 (.clk(clock), .D(or_4_out), .Q(x1_2));  // open: Qn, preset, en, reset
  D_Flip_Flop #(.trigger("rising")) d_ff_5 (.clk(clock), .D(and_9_out), .Q(x0_2));  // open: Qn, preset, en, reset
endmodule

module enable (
  input  sign,
  input  x4,
  input  x3,
  input  x2,
  input  x1,
  input  x0,
  input  enable,
  input  side,
  output change,
  output y4,
  output y3,
  output y2,
  output y1,
  output y0
);

  wire or_1_out, xor_1_out;

  and and_1 (y4, x4, enable);
  and and_2 (y3, x3, enable);
  and and_3 (y2, x2, enable);
  and and_4 (y1, x1, enable);
  and and_5 (y0, x0, enable);
  and and_6 (change, xor_1_out, or_1_out);
  xor xor_1 (xor_1_out, sign, x4);
  or or_1 (or_1_out, enable, side);

  // Notes on the sheet:
  //   Permite ou nao que um numero de 5 bits
  //   passe. Tambem avisa se o sinal do numero que
  //   passou e' diferente do sinal recebido quando sua
  //   passagem e'  permitida ou quando ele esta' 'a
  //   direita do bits mais significativo
endmodule

module muxsignal (
  input  x4,
  input  x3,
  input  x2,
  input  x1,
  input  x0,
  input  signal,
  output s4,
  output s3,
  output s2,
  output s1,
  output s0
);

  wire neg_1_y0, neg_1_y1, neg_1_y2, neg_1_y3, neg_1_y4;

  neg neg_1 (
    .x4(x4), .x3(x3), .x2(x2), .x1(x1), .x0(x0), .y4(neg_1_y4), .y3(neg_1_y3), .y2(neg_1_y2), .y1(neg_1_y1),
    .y0(neg_1_y0));
  mux2 mux2_1 (.a(x4), .b(neg_1_y4), .selector(signal), .out_4(s4));
  mux2 mux2_2 (.a(x3), .b(neg_1_y3), .selector(signal), .out_4(s3));
  mux2 mux2_3 (.a(x2), .b(neg_1_y2), .selector(signal), .out_4(s2));
  mux2 mux2_4 (.a(x1), .b(neg_1_y1), .selector(signal), .out_4(s1));
  mux2 mux2_5 (.a(x0), .b(neg_1_y0), .selector(signal), .out_4(s0));

  // Notes on the sheet:
  //   Multiplexador que seleciona o sinal do numero
endmodule

module mux2 (
  input  a,
  input  b,
  input  selector,
  output out_4
);

  wire and_1_out, and_2_out, not_1_out;

  not not_1 (not_1_out, selector);
  and and_1 (and_1_out, a, not_1_out);
  and and_2 (and_2_out, b, selector);
  or or_1 (out_4, and_1_out, and_2_out);

  // Notes on the sheet:
  //   Multiplexador que seleciona dois bits
endmodule

module innermul (
  input  a4,
  input  a3,
  input  a2,
  input  a1,
  input  a0,
  input  b4,
  input  b3,
  input  b2,
  input  b1,
  input  b0,
  output out_11,
  output out_12,
  output out_13,
  output out_14,
  output out_15,
  output out_16
);

  wire enable_1_change, enable_1_y0, enable_1_y1, enable_1_y2, enable_1_y3, enable_1_y4, enable_2_change,
       enable_2_y0, enable_2_y1, enable_2_y2, enable_2_y3, enable_2_y4, enable_3_change, enable_3_y0,
       enable_3_y1, enable_3_y2, enable_3_y3, enable_3_y4, enable_4_change, enable_4_y0, enable_4_y1,
       enable_4_y2, enable_4_y3, enable_4_y4, enable_5_change, enable_5_y0, enable_5_y1, enable_5_y2,
       enable_5_y3, enable_5_y4, or_1_out, or_2_out, or_3_out, or_4_out, or_5_out, sum_1_overflow, sum_1_s0,
       sum_1_s1, sum_1_s2, sum_1_s3, sum_1_s4, sum_2_overflow, sum_2_s0, sum_2_s1, sum_2_s2, sum_2_s3,
       sum_2_s4, sum_3_overflow, sum_3_s0, sum_3_s1, sum_3_s2, sum_3_s3, sum_3_s4, sum_4_overflow;

  enable enable_1 (
    .x4(a0), .x3(1'b0), .x2(1'b0), .x1(1'b0), .x0(1'b0), .sign(a4), .enable(b4), .side(b4),
    .change(enable_1_change), .y4(enable_1_y4), .y3(enable_1_y3), .y2(enable_1_y2), .y1(enable_1_y1),
    .y0(enable_1_y0));
  or or_1 (or_1_out, b4, b3);
  enable enable_2 (
    .x4(a2), .x3(a1), .x2(a0), .x1(1'b0), .x0(1'b0), .sign(a4), .enable(b2), .side(or_2_out),
    .change(enable_2_change), .y4(enable_2_y4), .y3(enable_2_y3), .y2(enable_2_y2), .y1(enable_2_y1),
    .y0(enable_2_y0));
  enable enable_3 (
    .x4(a1), .x3(a0), .x2(1'b0), .x1(1'b0), .x0(1'b0), .sign(a4), .enable(b3), .side(or_1_out),
    .change(enable_3_change), .y4(enable_3_y4), .y3(enable_3_y3), .y2(enable_3_y2), .y1(enable_3_y1),
    .y0(enable_3_y0));
  or or_2 (or_2_out, or_1_out, b2);
  enable enable_4 (
    .x4(a4), .x3(a3), .x2(a2), .x1(a1), .x0(a0), .sign(a4), .enable(b0), .side(or_4_out),
    .change(enable_4_change), .y4(enable_4_y4), .y3(enable_4_y3), .y2(enable_4_y2), .y1(enable_4_y1),
    .y0(enable_4_y0));
  enable enable_5 (
    .x4(a3), .x3(a2), .x2(a1), .x1(a0), .x0(1'b0), .sign(a4), .enable(b1), .side(or_3_out),
    .change(enable_5_change), .y4(enable_5_y4), .y3(enable_5_y3), .y2(enable_5_y2), .y1(enable_5_y1),
    .y0(enable_5_y0));
  or or_3 (or_3_out, or_2_out, b1);
  or or_4 (or_4_out, or_3_out, b0);
  sum sum_1 (
    .a4(enable_3_y4), .a3(enable_3_y3), .a2(enable_3_y2), .a1(enable_3_y1), .a0(enable_3_y0),
    .b4(enable_1_y4), .b3(enable_1_y3), .b2(enable_1_y2), .b1(enable_1_y1), .b0(enable_1_y0),
    .OVERFLOW(sum_1_overflow), .s4(sum_1_s4), .s3(sum_1_s3), .s2(sum_1_s2), .s1(sum_1_s1), .s0(sum_1_s0));  // open: carry
  or or_5 (or_5_out, enable_4_change, enable_5_change, enable_2_change, enable_3_change, enable_1_change);
  sum sum_2 (
    .a4(enable_4_y4), .a3(enable_4_y3), .a2(enable_4_y2), .a1(enable_4_y1), .a0(enable_4_y0),
    .b4(enable_5_y4), .b3(enable_5_y3), .b2(enable_5_y2), .b1(enable_5_y1), .b0(enable_5_y0),
    .OVERFLOW(sum_2_overflow), .s4(sum_2_s4), .s3(sum_2_s3), .s2(sum_2_s2), .s1(sum_2_s1), .s0(sum_2_s0));  // open: carry
  sum sum_3 (
    .a4(enable_2_y4), .a3(enable_2_y3), .a2(enable_2_y2), .a1(enable_2_y1), .a0(enable_2_y0), .b4(sum_1_s4),
    .b3(sum_1_s3), .b2(sum_1_s2), .b1(sum_1_s1), .b0(sum_1_s0), .OVERFLOW(sum_3_overflow), .s4(sum_3_s4),
    .s3(sum_3_s3), .s2(sum_3_s2), .s1(sum_3_s1), .s0(sum_3_s0));  // open: carry
  sum sum_4 (
    .a4(sum_2_s4), .a3(sum_2_s3), .a2(sum_2_s2), .a1(sum_2_s1), .a0(sum_2_s0), .b4(sum_3_s4), .b3(sum_3_s3),
    .b2(sum_3_s2), .b1(sum_3_s1), .b0(sum_3_s0), .OVERFLOW(sum_4_overflow), .s4(out_11), .s3(out_12),
    .s2(out_13), .s1(out_14), .s0(out_15));  // open: carry
  or or_6 (out_16, sum_4_overflow, sum_2_overflow, sum_3_overflow, sum_1_overflow, or_5_out);

  // Notes on the sheet:
  //   Calcula a multiplicacao de dois numeros de 5 bits positivos ou
  //   de um positivo com um negativo, nessa ordem.
endmodule
